// Logisim project cpu.circ as structural Verilog: 9 circuits, main circuit main
module main (
  input  in_1,
  output [15:0] out_2,
  output [15:0] out_3,
  output [4:0] out_4,
  output [3:0] out_5
);

  wire clock_1_out, clock_2_out, clock_3_out, clock_4_out, dec_1_nextbyte, instrbuffer_1_ldimm, not_1_out;
  wire [1:0] dec_1_rega, dec_1_regb, decoder_1_out0, decoder_2_out0, instrbuffer_1_qa, instrbuffer_1_qb;
  wire [2:2] decoder_1_out2, decoder_2_out2;
  wire [3:3] decoder_1_out3, decoder_2_out3;
  wire [4:0] dec_1_code;
  wire [15:0] adder_1_out, controlled_buffer_1_out, controlled_buffer_2_out, flags_q, multiplexer_1_out,
       pc_q, r0_q, r1_q, r2_q, r3_q, rom_1_data;

  ROM #(.addrWidth(16), .dataWidth(16)) rom_1 (.addr(pc_q), .data(rom_1_data));
  Register #(.width(16)) pc (.D(adder_1_out), .clk(clock_1_out), .Q(pc_q), .clr(in_1));  // open: en
  Clock clock_1 (.out(clock_1_out));
  Adder #(.width(16)) adder_1 (.a(pc_q), .b(16'h1), .out(adder_1_out));  // open: cin, cout
  dec dec_1 (
    .instr(rom_1_data[11:0]), .nextByte(dec_1_nextbyte), .regA(dec_1_rega), .regB(dec_1_regb),
    .code(dec_1_code));
  Clock clock_2 (.out(clock_2_out));
  Clock clock_3 (.out(clock_3_out));
  Decoder #(.select(2)) decoder_1 (
    .out0(decoder_1_out0[0]), .out1(decoder_1_out0[1]), .out2(decoder_1_out2[2]), .out3(decoder_1_out3[3]),
    .sel(instrbuffer_1_qa));  // open: en
  instrBuffer instrbuffer_1 (
    .RegA(dec_1_rega), .RegB(dec_1_regb), .Instr(dec_1_code), .R(in_1), .CLK(clock_2_out),
    .Imm(dec_1_nextbyte), .FLAGS(rom_1_data[15:12]), .Qflags(out_5), .Qa(instrbuffer_1_qa),
    .Qb(instrbuffer_1_qb), .Qinstr(out_4), .LDImm(instrbuffer_1_ldimm));
  Register #(.width(16)) r0 (.D(out_3), .en(decoder_1_out0[0]), .clk(clock_3_out), .Q(r0_q), .clr(in_1));
  Register #(.width(16)) r1 (.D(out_3), .en(decoder_1_out0[1]), .clk(clock_3_out), .Q(r1_q), .clr(in_1));
  Register #(.width(16)) r2 (.D(out_3), .en(decoder_1_out2[2]), .clk(clock_3_out), .Q(r2_q), .clr(in_1));
  Register #(.width(16)) r3 (.D(out_3), .en(decoder_1_out3[3]), .clk(clock_3_out), .Q(r3_q), .clr(in_1));
  Decoder #(.select(2)) decoder_2 (
    .out0(decoder_2_out0[0]), .out1(decoder_2_out0[1]), .out2(decoder_2_out2[2]), .out3(decoder_2_out3[3]),
    .sel(instrbuffer_1_qb));  // open: en
  assign controlled_buffer_1_out = decoder_1_out0[0] ? r0_q : 16'bz;  // Controlled_Buffer controlled_buffer_1
  assign controlled_buffer_2_out = decoder_2_out0[0] ? r0_q : 16'bz;  // Controlled_Buffer controlled_buffer_2
  assign controlled_buffer_1_out = decoder_1_out0[1] ? r1_q : 16'bz;  // Controlled_Buffer controlled_buffer_3
  assign controlled_buffer_2_out = decoder_2_out0[1] ? r1_q : 16'bz;  // Controlled_Buffer controlled_buffer_4
  assign controlled_buffer_1_out = decoder_1_out2[2] ? r2_q : 16'bz;  // Controlled_Buffer controlled_buffer_5
  assign controlled_buffer_2_out = decoder_2_out2[2] ? r2_q : 16'bz;  // Controlled_Buffer controlled_buffer_6
  assign controlled_buffer_1_out = decoder_1_out3[3] ? r3_q : 16'bz;  // Controlled_Buffer controlled_buffer_7
  assign controlled_buffer_2_out = decoder_2_out3[3] ? r3_q : 16'bz;  // Controlled_Buffer controlled_buffer_8
  Register #(.width(16)) lr ();  // open: D, en, clk, Q, clr
  Register #(.width(16)) sp ();  // open: D, en, clk, Q, clr
  Multiplexer #(.width(16)) multiplexer_1 (
    .in0(rom_1_data), .in1(controlled_buffer_2_out), .out(multiplexer_1_out), .sel(not_1_out));
  not not_1 (not_1_out, instrbuffer_1_ldimm);
  Clock clock_4 (.out(clock_4_out));
  Register #(.width(16)) flags (.D(out_2), .en(1'b1), .clk(clock_4_out), .Q(flags_q), .clr(in_1));
  alu alu_1 (
    .A(controlled_buffer_1_out), .B(multiplexer_1_out), .Cond(out_5), .F(flags_q), .S(out_4), .Q(out_3),
    .FQ(out_2));

  // Other names for the same wires on the sheet: CLR = in_1

  // Notes on the sheet:
  //   contents of rom_1 (hex, n*v repeats v):
  //   207 1 1c0 208 207 5 1001 21c0 1207 0 31c0 21c0
endmodule

module logicUnit (
  input  [15:0] A,
  input  [15:0] B,
  input  [2:0] S,
  output [15:0] Q
);

  wire [15:0] and_1_out, bit_extender_1_out, multiplexer_1_out, or_1_out, xor_1_out;

  assign bit_extender_1_out = {{15{S[2]}}, S[2]};  // Bit_Extender bit_extender_1
  assign and_1_out = A & B;  // AND_Gate and_1, 16 bits wide
  assign or_1_out = A | B;  // OR_Gate or_1, 16 bits wide
  Hex_Digit_Display hex_digit_display_1 (.value({1'b0, S}));  // open: dp
  assign xor_1_out = A ^ B;  // XOR_Gate xor_1, 16 bits wide
  Multiplexer #(.select(2), .width(16)) multiplexer_1 (
    .in0(and_1_out), .in1(or_1_out), .in2(xor_1_out), .in3(A), .out(multiplexer_1_out), .sel(S[1:0]));
  assign Q = multiplexer_1_out ^ bit_extender_1_out;  // XOR_Gate xor_2, 16 bits wide

  // Notes on the sheet:
  //   logic unit
  //   toggleable not
endmodule

module arithmaticUnit (
  input  [15:0] A,
  input  [15:0] B,
  input  [2:0] S,
  output [15:0] Q
);

  wire [15:0] adder_1_out, adder_2_out, multiplier_1_out, subtractor_1_out, subtractor_2_out;

  Hex_Digit_Display hex_digit_display_1 (.value({1'b0, S}));  // open: dp
  Adder #(.width(16)) adder_1 (.a(A), .b(B), .out(adder_1_out));  // open: cin, cout
  Subtractor #(.width(16)) subtractor_1 (.a(A), .b(B), .out(subtractor_1_out));  // open: bin, bout
  Adder #(.width(16)) adder_2 (.a(A), .b(16'h1), .out(adder_2_out));  // open: cin, cout
  Subtractor #(.width(16)) subtractor_2 (.a(A), .b(16'h1), .out(subtractor_2_out));  // open: bin, bout
  Multiplier #(.width(16)) multiplier_1 (.a(A), .b(B), .out(multiplier_1_out));  // open: cin, cout
  Multiplexer #(.select(3), .width(16)) multiplexer_1 (
    .in0(adder_1_out), .in1(subtractor_1_out), .in2(adder_2_out), .in3(subtractor_2_out),
    .in4(multiplier_1_out), .out(Q), .sel(S));  // open: in5, in6, in7

  // Notes on the sheet:
  //   a+b  a-b  a+1 a-1, a*b ?
endmodule

module alu (
  input  [15:0] A,
  input  [15:0] B,
  input  [4:0] S,
  input  [3:0] Cond,
  input  [15:0] F,
  output [15:0] Q,
  output [15:0] FQ
);

  wire and_1_out, and_2_out, and_4_out, demultiplexer_1_out0, demultiplexer_1_out1, demultiplexer_1_out2,
       demultiplexer_1_out3, not_1_out, not_2_out, or_1_out, or_2_out;
  wire [1:0] and_3_out, bit_extender_1_out;
  wire [15:0] arithmaticunit_1_q, flagupdater_1_q, logicunit_1_q;

  Demultiplexer #(.select(2)) demultiplexer_1 (
    .out0(demultiplexer_1_out0), .out1(demultiplexer_1_out1), .out2(demultiplexer_1_out2),
    .out3(demultiplexer_1_out3), .in(1'b1), .sel(S[4:3]));
  LED led_1 (.in(demultiplexer_1_out0));
  LED led_2 (.in(demultiplexer_1_out1));
  LED led_3 (.in(demultiplexer_1_out2));
  LED led_4 (.in(demultiplexer_1_out3));
  not not_1 (not_1_out, Cond[2]);
  and and_1 (and_1_out, Cond[2], F[14]);
  not not_2 (not_2_out, Cond[1]);
  and and_2 (and_2_out, Cond[1], F[15]);
  logicUnit logicunit_1 (.S(S[2:0]), .A(A), .B(B), .Q(logicunit_1_q));
  arithmaticUnit arithmaticunit_1 (.S(S[2:0]), .A(A), .B(B), .Q(arithmaticunit_1_q));
  or or_1 (or_1_out, not_1_out, and_1_out);
  or or_2 (or_2_out, not_2_out, and_2_out);
  Multiplexer #(.select(2), .width(16)) multiplexer_1 (
    .in0(A), .in1(B), .in2(logicunit_1_q), .in3(arithmaticunit_1_q), .out(Q), .sel(and_3_out));
  assign and_3_out = S[4:3] & bit_extender_1_out;  // AND_Gate and_3, 2 bits wide
  flagUpdater flagupdater_1 (.Res(Q), .Q(flagupdater_1_q));
  and and_4 (and_4_out, or_1_out, or_2_out);
  Multiplexer #(.width(16)) multiplexer_2 (.in0(F), .in1(flagupdater_1_q), .out(FQ), .sel(Cond[0]));
  assign bit_extender_1_out = {{1{and_4_out}}, and_4_out};  // Bit_Extender bit_extender_1

  // Notes on the sheet:
  //   neg flag conditional
  //   zero flag conditional
  //   if low pass A
endmodule

module flagUpdater (
  input  [15:0] Res,
  output [15:0] Q
);

  Comparator #(.width(16)) comparator_1 (.a(Res), .b({16{1'b0}}), .eq(Q[15]), .lt(Q[14]));  // open: gt

  assign Q[13:0] = {14{1'b0}};
endmodule

module dec (
  input  [11:0] instr,
  output nextByte,
  output [1:0] regA,
  output [1:0] regB,
  output [4:0] code
);

  wire [2:0] instrtype_1_q;
  wire [3:0] bit_extender_1_out, bit_extender_2_out, bit_extender_3_out, bit_extender_4_out,
       bit_extender_5_out, multiplexer_3_out;

  and and_1 (nextByte, instr[0], instr[1], instr[2]);
  instrType instrtype_1 (.T(instr), .Q(instrtype_1_q));
  assign bit_extender_1_out = {{1{1'b0}}, instr[5:3]};  // Bit_Extender bit_extender_1
  assign bit_extender_2_out = {{2{1'b0}}, instr[6:5]};  // Bit_Extender bit_extender_2
  assign bit_extender_3_out = {{2{1'b0}}, instr[5:4]};  // Bit_Extender bit_extender_3
  Multiplexer #(.select(3), .width(2)) multiplexer_1 (
    .in0(instr[1:0]), .in1(instr[4:3]), .in2(instr[4:3]), .in3(instr[4:3]), .in4(instr[1:0]), .out(regA),
    .sel(instrtype_1_q));  // open: in5, in6, in7
  Multiplexer #(.select(3), .width(2)) multiplexer_2 (
    .in1(instr[1:0]), .in2(instr[1:0]), .in3(instr[1:0]), .out(regB), .sel(instrtype_1_q));  // open: in0, in4, in5, in6, in7
  Multiplexer #(.select(3), .width(4)) multiplexer_3 (
    .in0(bit_extender_1_out), .in1(instr[8:5]), .in2(bit_extender_2_out), .in3(bit_extender_3_out),
    .out(multiplexer_3_out), .sel(instrtype_1_q));  // open: in4, in5, in6, in7
  Hex_Digit_Display hex_digit_display_1 (.value(multiplexer_3_out));  // open: dp
  assign bit_extender_4_out = {{2{1'b0}}, regA};  // Bit_Extender bit_extender_4
  assign bit_extender_5_out = {{2{1'b0}}, regB};  // Bit_Extender bit_extender_5
  Hex_Digit_Display hex_digit_display_2 (.value(bit_extender_4_out));  // open: dp
  Hex_Digit_Display hex_digit_display_3 (.value(bit_extender_5_out));  // open: dp
  Pull_Resistor pull_resistor_1 (.node(regB));
  instrDec instrdec_1 (.InstrIndex(multiplexer_3_out), .InstrType(instrtype_1_q), .Q(code));
endmodule

module instrType (
  input  [11:0] T,
  output [2:0] Q
);

  wire and_1_out, and_2_out, and_3_out, and_4_out, and_5_out, and_6_out, and_7_out;

  and and_1 (and_1_out, T[6], T[7], T[8], and_2_out);
  and and_2 (and_2_out, ~T[9], ~T[10], ~T[11]);  // AND_Gate
  and and_3 (and_3_out, ~T[7], ~T[8], T[9], ~T[10], ~T[11]);  // AND_Gate
  and and_4 (and_4_out, T[7], ~T[8], T[9], ~T[10], ~T[11]);  // AND_Gate
  and and_5 (and_5_out, ~T[6], ~T[7], T[8], T[9], ~T[10], ~T[11]);  // AND_Gate
  and and_6 (and_6_out, ~T[0], T[1], T[2], T[3], T[4], T[5], T[6], T[7], T[8], T[9], T[10], T[11]);  // AND_Gate
  and and_7 (and_7_out, ~and_1_out, and_2_out);  // AND_Gate
  Priority_Encoder priority_encoder_1 (
    .in0(and_1_out), .in1(and_7_out), .in2(and_3_out), .in3(and_4_out), .in4(and_5_out), .in5(and_6_out),
    .out(Q));  // open: in6, in7, en_in, gs, en_out
  Hex_Digit_Display hex_digit_display_1 (.value({1'b0, Q}));  // open: dp

  // Notes on the sheet:
  //   move instruction
  //   ram move
  //   stack
  //   jump
  //   math single arg
  //   math with double args
endmodule

module instrDec (
  input  [3:0] InstrIndex,
  input  [2:0] InstrType,
  output [4:0] Q
);

  ROM #(.addrWidth(7), .dataWidth(5)) rom_1 (.addr({InstrType, InstrIndex}), .data(Q));

  // Notes on the sheet:
  //   contents of rom_1 (hex, n*v repeats v):
  //   1a 1b 17 13*0 18 19 1c 10 11 12 19 9*0 8
endmodule

module instrBuffer (
  input  CLK,
  input  [1:0] RegA,
  input  [1:0] RegB,
  input  [4:0] Instr,
  input  Imm,
  input  [3:0] FLAGS,
  input  R,
  output [1:0] Qa,
  output [1:0] Qb,
  output [4:0] Qinstr,
  output LDImm,
  output [3:0] Qflags
);

  wire BitBuffer2_q, not_1_out;
  wire [3:0] bit_extender_1_out, bit_extender_2_out;
  wire [8:0] InstructionBuffer_q;

  Register #(.width(9)) InstructionBuffer (
    .D({Instr, RegB, RegA}), .en(not_1_out), .clk(CLK), .Q(InstructionBuffer_q), .clr(R));
  LED led_1 (.in(not_1_out));
  Register #(.width(1)) BitBuffer (.D(Imm), .clk(CLK), .Q(LDImm), .clr(R));  // open: en
  Register #(.width(4)) FlagBuffer (.D(FLAGS), .en(not_1_out), .clk(CLK), .Q(Qflags), .clr(R));
  not not_1 (not_1_out, LDImm);
  Register #(.width(1)) BitBuffer2 (.D(LDImm), .clk(CLK), .Q(BitBuffer2_q), .clr(R));  // open: en
  Multiplexer #(.width(9)) multiplexer_1 (
    .in0(InstructionBuffer_q), .in1({9{1'b0}}), .out({Qinstr, Qb, Qa}), .sel(BitBuffer2_q));
  LED led_2 (.in(BitBuffer2_q));
  Hex_Digit_Display hex_digit_display_1 (.value(bit_extender_1_out));  // open: dp
  Hex_Digit_Display hex_digit_display_2 (.value(bit_extender_2_out));  // open: dp
  assign bit_extender_1_out = {{2{1'b0}}, Qa};  // Bit_Extender bit_extender_1
  assign bit_extender_2_out = {{2{1'b0}}, Qb};  // Bit_Extender bit_extender_2

  // Notes on the sheet:
  //   dont load if bitbuf 1
  //   execute nop if Im or bitbuf2
endmodule
